# Fritzing sketch plug-bot (saved by Fritzing 0.9.3b)

parts:
  Part4 = NRF24L01+ Breakout Board
  S2 = Pushbutton [package="[SMD]"]
  Part5 = Arduino Nano (Rev3.0) (ICSP)
  J2 = Piezo Speaker
  U1 = RELAY [package=relay-g5q]
  Current_Sensor1 = ACS-715
  U3 = SWITCH_SPDT [package=kps-1290]

nets:
  GND: Part4.GND, S2.Pin_3, S2.Pin_4, Part5.GND, J2.pin1, U1.NO, Current_Sensor1.GND
  VCC: Part4.VCC, Part5.3V3
  N1: Part4.CE, Part5.D7
  N2: Part4.CS, Part5.D8
  N3: Part4.SCK, Part5.D13/SCK
  N4: Part4.MOSI, Part5.D11/MOSI
  N5: Part4.MISO, Part5.D12/MISO
  N6: Part4.IRQ, Part5.D2
  N7: S2.Pin_1, Part5.D3
  N8: Part5.D4, U1.NC
  N9: Part5.D6, J2.pin2
  N10: Part5.VIN, U3.P
  5V: Part5.5V, Current_Sensor1.Vcc
  N11: Part5.A0, Current_Sensor1.VIOUT
  N12: U1.COIL2, Current_Sensor1.IP–

notes:
  5V
  220V
  Plug

custom parts:
  ACS-715: Breakout Board with ACS 714/715 Hall Effect-Based Linear Current Sensor from Pololu This board is a simple carrier for Allegro’s 30A ACS 714/715 Hall effect-based linear current sensor. This version accepts a unidirectional current input up to 30 A. The output is an analog voltage (133 mV/A) that reads 500 mV for no input current and has a typical error of less than 1.5%.
